# Fritzing sketch hackdads-pebble-altimeter-smart-strap (saved by Fritzing 0.9.2b)
breadboards: 1

parts:
  Teensy_3_1 = Teensy 3.1  # not connected
  JP1 = Header 6 [package=1x06-smd]
  U1 = MPL3115A2 [package=lga8]
  R1 = Resistor [tolerance=±5% resistance=10k package="0805 [SMD]"]

nets:
  N1: JP1.1, U1.VDD, R1.Pin_1
  N2: JP1.2, R1.Pin_0
  N3: JP1.3, U1.GND

notes:
  Pin 1 -> Pebble Time Power
  Pin 2 -> Pebble Time Data
  Pin 3 -> Pebble Time Ground
  Wiring
  Red -> Power (3.3V)
  Black -> Ground
  Pink -> I2C SDA
  Orange -> I2C SCL
  Header to Pebble Time
  Teensy 3.1
  Freescale
  MPL3115A2
